// Logisim project release.circ as structural Verilog
module SUBCIRC_MatrixMultiplier (
  input  [63:0] B0,
  input  [63:0] A0,
  input  [63:0] B1,
  input  [63:0] A1,
  input  [63:0] B2,
  input  [63:0] A2,
  input  [63:0] B3,
  input  [63:0] A3,
  output [63:0] S0,
  output [63:0] S1,
  output [63:0] S2,
  output [63:0] S3,
  output [63:0] W0,
  output [63:0] W1,
  output [63:0] W2,
  output [63:0] W3
);

  Multiplier #(.width(64)) multiplier_1 (.a(A0), .b(B0), .out(S0));  // open: cin, cout
  Multiplier #(.width(64)) multiplier_2 (.a(A0), .b(B1), .out(S1));  // open: cin, cout
  Multiplier #(.width(64)) multiplier_3 (.a(A2), .b(B0), .out(S2));  // open: cin, cout
  Multiplier #(.width(64)) multiplier_4 (.a(A2), .b(B1), .out(S3));  // open: cin, cout
  Multiplier #(.width(64)) multiplier_5 (.a(A1), .b(B2), .out(W0));  // open: cin, cout
  Multiplier #(.width(64)) multiplier_6 (.a(A1), .b(B3), .out(W1));  // open: cin, cout
  Multiplier #(.width(64)) multiplier_7 (.a(A3), .b(B2), .out(W2));  // open: cin, cout
  Multiplier #(.width(64)) multiplier_8 (.a(A3), .b(B3), .out(W3));  // open: cin, cout

  // Notes on the sheet:
  //   Acts as a Partial Multiplication Node
  //   Supports Partial Matrix Multiplication where A*B = S1, S2 where S = S1+S2
  //   A0B0
  //   A0B1
  //   A2B0
  //   A2B1
  //   A1B2
  //   A1B3
  //   A3B2
  //   A3B3
endmodule

module RAMControllerRAW (
  input  [7:0] rs,
  input  [7:0] rd,
  input  CLK,
  output [7:0] A,
  output WE,
  output OE
);

  D_Flip_Flop d_ff_1 (.clk(CLK), .D(1'b1), .Q(WE));  // open: Qn, preset, reset
  not not_1 (OE, CLK);
  Multiplexer #(.width(8)) multiplexer_1 (.in0(rs), .in1(rd), .out(A), .sel(CLK));
endmodule

module SUBCIRC_RAMBank (
  input  [63:0] D3,
  input  [63:0] D2,
  input  [63:0] D1,
  input  [63:0] D0,
  input  [7:0] Address,
  input  WE,
  input  OE,
  input  CLK,
  output [63:0] S3,
  output [63:0] S2,
  output [63:0] S1,
  output [63:0] S0
);

  RAM #(.dataWidth(64), .\type ("nonvolatile")) C1 (.addr(Address), .we(WE), .oe(OE), .clk(CLK), .din(D0), .dout(S0));
  RAM #(.dataWidth(64), .\type ("nonvolatile")) ram_1 (
    .addr(Address), .we(WE), .oe(OE), .clk(CLK), .din(D1), .dout(S1));
  RAM #(.dataWidth(64), .\type ("nonvolatile")) ram_2 (
    .addr(Address), .we(WE), .oe(OE), .clk(CLK), .din(D2), .dout(S2));
  RAM #(.dataWidth(64), .\type ("nonvolatile")) ram_3 (
    .addr(Address), .we(WE), .oe(OE), .clk(CLK), .din(D3), .dout(S3));
endmodule

module Assembly (
);

  wire CLOCK_GLOBAL, comparator_2_eq, comparator_3_eq, undriven_2, undriven_3, undriven_4;
  wire [7:0] counter_4_q, counter_5_q, RAM_A_ADDRESS, RAM_B_ADDRESS;
  wire [15:0] bit_extender_1_out, bit_extender_2_out, COL_ITERCOUNT, RAM_S_ADDRESS, register_5_q,
       ROW_ITERCOUNT, undriven;
  wire [63:0] register_1_q, register_2_q, register_3_q, register_4_q, S0, S1, S2, S3,
       subcirc_matrixadder_1_s0, subcirc_matrixadder_1_s1, subcirc_matrixadder_1_s2,
       subcirc_matrixadder_1_s3, subcirc_matrixadder_2_s0, subcirc_matrixadder_2_s1,
       subcirc_matrixadder_2_s2, subcirc_matrixadder_2_s3, subcirc_matrixadder_3_s0,
       subcirc_matrixadder_3_s1, subcirc_matrixadder_3_s2, subcirc_matrixadder_3_s3, subcirc_rambank_1_s0,
       subcirc_rambank_1_s1, subcirc_rambank_1_s2, subcirc_rambank_1_s3, subcirc_rambank_2_s0,
       subcirc_rambank_2_s1, subcirc_rambank_2_s2, subcirc_rambank_2_s3, subcirc_rambank_3_s0,
       subcirc_rambank_3_s1, subcirc_rambank_3_s2, subcirc_rambank_3_s3, subcirc_rambank_4_s0,
       subcirc_rambank_4_s1, subcirc_rambank_4_s2, subcirc_rambank_4_s3, test_subcirc_matrixmultiplier_1_s0,
       test_subcirc_matrixmultiplier_1_s1, test_subcirc_matrixmultiplier_1_s2,
       test_subcirc_matrixmultiplier_1_s3, test_subcirc_matrixmultiplier_1_w0,
       test_subcirc_matrixmultiplier_1_w1, test_subcirc_matrixmultiplier_1_w2,
       test_subcirc_matrixmultiplier_1_w3, test_subcirc_matrixmultiplier_2_s0,
       test_subcirc_matrixmultiplier_2_s1, test_subcirc_matrixmultiplier_2_s2,
       test_subcirc_matrixmultiplier_2_s3, test_subcirc_matrixmultiplier_2_w0,
       test_subcirc_matrixmultiplier_2_w1, test_subcirc_matrixmultiplier_2_w2,
       test_subcirc_matrixmultiplier_2_w3, undriven_5, undriven_6, undriven_7, undriven_8;

  Counter #(.max('hffff), .width(16)) counter_1 (
    .count(1'b1), .Q(RAM_S_ADDRESS), .up(1'b1), .clk(CLOCK_GLOBAL));  // open: load, D, carry, clr
  Counter counter_2 (.count(1'b1), .Q(RAM_A_ADDRESS), .up(1'b1), .clk(CLOCK_GLOBAL));  // open: load, D, carry, clr
  Comparator #(.mode("unsigned"), .width(16)) comparator_1 (.a(undriven), .b(RAM_S_ADDRESS));  // open: gt, eq, lt
  Counter counter_3 (.count(1'b1), .Q(RAM_B_ADDRESS), .up(1'b1), .clk(CLOCK_GLOBAL));  // open: load, D, carry, clr
  // Probe on S0
  // Probe on S2
  // Probe on RAM_B_ADDRESS
  // Probe on RAM_A_ADDRESS
  // Probe on S1
  // Probe on S3
  // Probe on subcirc_rambank_1_s0
  SUBCIRC_RAMBank subcirc_rambank_1 (
    .Address(RAM_A_ADDRESS), .OE(1'b1), .CLK(CLOCK_GLOBAL), .S3(subcirc_rambank_1_s3),
    .S2(subcirc_rambank_1_s2), .S1(subcirc_rambank_1_s1), .S0(subcirc_rambank_1_s0));  // open: D3, D2, D1, D0, WE
  SUBCIRC_RAMBank subcirc_rambank_2 (
    .Address(RAM_A_ADDRESS), .OE(1'b1), .CLK(CLOCK_GLOBAL), .S3(subcirc_rambank_2_s3),
    .S2(subcirc_rambank_2_s2), .S1(subcirc_rambank_2_s1), .S0(subcirc_rambank_2_s0));  // open: D3, D2, D1, D0, WE
  // Probe on subcirc_rambank_1_s0
  // Probe on subcirc_matrixadder_2_s3
  // Probe on subcirc_matrixadder_2_s1
  SUBCIRC_MatrixAdder subcirc_matrixadder_1 (
    .B0(test_subcirc_matrixmultiplier_1_s0), .A0(test_subcirc_matrixmultiplier_1_w0),
    .B1(test_subcirc_matrixmultiplier_1_s1), .A1(test_subcirc_matrixmultiplier_1_w1),
    .B2(test_subcirc_matrixmultiplier_1_s2), .A2(test_subcirc_matrixmultiplier_1_w2),
    .B3(test_subcirc_matrixmultiplier_1_s3), .A3(test_subcirc_matrixmultiplier_1_w3),
    .S0(subcirc_matrixadder_1_s0), .S1(subcirc_matrixadder_1_s1), .S2(subcirc_matrixadder_1_s2),
    .S3(subcirc_matrixadder_1_s3));
  SUBCIRC_MatrixAdder subcirc_matrixadder_2 (
    .S0(subcirc_matrixadder_2_s0), .S1(subcirc_matrixadder_2_s1), .S2(subcirc_matrixadder_2_s2),
    .S3(subcirc_matrixadder_2_s3));  // open: B0, A0, B1, A1, B2, A2, B3, A3
  TEST_SUBCIRC_MatrixMultiplier test_subcirc_matrixmultiplier_1 (
    .B3(subcirc_rambank_4_s3), .B2(subcirc_rambank_4_s2), .B1(subcirc_rambank_4_s1),
    .B0(subcirc_rambank_4_s0), .A3(subcirc_rambank_2_s3), .A2(subcirc_rambank_2_s2),
    .A1(subcirc_rambank_2_s1), .A0(subcirc_rambank_2_s0), .S0(test_subcirc_matrixmultiplier_1_s0),
    .W0(test_subcirc_matrixmultiplier_1_w0), .S1(test_subcirc_matrixmultiplier_1_s1),
    .W1(test_subcirc_matrixmultiplier_1_w1), .S2(test_subcirc_matrixmultiplier_1_s2),
    .W2(test_subcirc_matrixmultiplier_1_w2), .S3(test_subcirc_matrixmultiplier_1_s3),
    .W3(test_subcirc_matrixmultiplier_1_w3));
  TEST_SUBCIRC_MatrixAdder test_subcirc_matrixadder_1 (
    .B0(subcirc_matrixadder_3_s0), .B1(subcirc_matrixadder_3_s1), .B2(subcirc_matrixadder_3_s2),
    .B3(subcirc_matrixadder_3_s3), .A0(subcirc_matrixadder_1_s0), .A1(subcirc_matrixadder_1_s1),
    .A2(subcirc_matrixadder_1_s2), .A3(subcirc_matrixadder_1_s3), .S0(S0), .S1(S1), .S2(S2), .S3(S3));
  SUBCIRC_RAMBank subcirc_rambank_3 (
    .Address(RAM_B_ADDRESS), .OE(1'b1), .CLK(CLOCK_GLOBAL), .S3(subcirc_rambank_3_s3),
    .S2(subcirc_rambank_3_s2), .S1(subcirc_rambank_3_s1), .S0(subcirc_rambank_3_s0));  // open: D3, D2, D1, D0, WE
  SUBCIRC_RAMBank subcirc_rambank_4 (
    .Address(RAM_B_ADDRESS), .OE(1'b1), .CLK(CLOCK_GLOBAL), .S3(subcirc_rambank_4_s3),
    .S2(subcirc_rambank_4_s2), .S1(subcirc_rambank_4_s1), .S0(subcirc_rambank_4_s0));  // open: D3, D2, D1, D0, WE
  TEST_SUBCIRC_MatrixMultiplier test_subcirc_matrixmultiplier_2 (
    .B3(subcirc_rambank_3_s3), .B2(subcirc_rambank_3_s2), .B1(subcirc_rambank_3_s1),
    .B0(subcirc_rambank_3_s0), .A3(subcirc_rambank_1_s3), .A2(subcirc_rambank_1_s2),
    .A1(subcirc_rambank_1_s1), .A0(subcirc_rambank_1_s0), .S0(test_subcirc_matrixmultiplier_2_s0),
    .W0(test_subcirc_matrixmultiplier_2_w0), .S1(test_subcirc_matrixmultiplier_2_s1),
    .W1(test_subcirc_matrixmultiplier_2_w1), .S2(test_subcirc_matrixmultiplier_2_s2),
    .W2(test_subcirc_matrixmultiplier_2_w2), .S3(test_subcirc_matrixmultiplier_2_s3),
    .W3(test_subcirc_matrixmultiplier_2_w3));
  SUBCIRC_MatrixAdder subcirc_matrixadder_3 (
    .B0(test_subcirc_matrixmultiplier_2_s0), .A0(test_subcirc_matrixmultiplier_2_w0),
    .B1(test_subcirc_matrixmultiplier_2_s1), .A1(test_subcirc_matrixmultiplier_2_w1),
    .B2(test_subcirc_matrixmultiplier_2_s2), .A2(test_subcirc_matrixmultiplier_2_w2),
    .B3(test_subcirc_matrixmultiplier_2_s3), .A3(test_subcirc_matrixmultiplier_2_w3),
    .S0(subcirc_matrixadder_3_s0), .S1(subcirc_matrixadder_3_s1), .S2(subcirc_matrixadder_3_s2),
    .S3(subcirc_matrixadder_3_s3));
  // Probe on subcirc_matrixadder_2_s2
  // Probe on subcirc_matrixadder_2_s0
  Register #(.width(64)) register_1 (.D(S0), .en(undriven_2), .Q(register_1_q), .clk(undriven_3), .clr(undriven_4));
  Register #(.width(64)) register_2 (.D(S1), .en(undriven_2), .Q(register_2_q), .clk(undriven_3), .clr(undriven_4));
  Register #(.width(64)) register_3 (.D(S2), .en(undriven_2), .Q(register_3_q), .clk(undriven_3), .clr(undriven_4));
  Register #(.width(64)) register_4 (.D(S3), .en(undriven_2), .Q(register_4_q), .clk(undriven_3), .clr(undriven_4));
  Register #(.width(16)) register_5 (.D(RAM_S_ADDRESS), .en(1'b1), .Q(register_5_q), .clk(CLOCK_GLOBAL));  // open: clr
  Clock clock_1 (.out(CLOCK_GLOBAL));
  SUBCIRC_RAMBankOutput subcirc_rambankoutput_1 (
    .D3(undriven_5), .D2(undriven_6), .D1(undriven_7), .D0(undriven_8), .Address(register_5_q),
    .CLK(CLOCK_GLOBAL));  // open: WE, OE, S3, S2, S1, S0
  assign bit_extender_1_out = {{8{counter_4_q[7]}}, counter_4_q};  // Bit_Extender bit_extender_1
  Counter counter_4 (.Q(counter_4_q));  // open: load, D, count, carry, up, clk, clr
  assign bit_extender_2_out = {{8{counter_5_q[7]}}, counter_5_q};  // Bit_Extender bit_extender_2
  Counter counter_5 (.Q(counter_5_q));  // open: load, D, count, carry, up, clk, clr
  Comparator #(.width(16)) comparator_2 (
    .a(bit_extender_1_out), .b(ROW_ITERCOUNT), .eq(comparator_2_eq));  // open: gt, lt
  Comparator #(.width(16)) comparator_3 (
    .a(bit_extender_2_out), .b(COL_ITERCOUNT), .eq(comparator_3_eq));  // open: gt, lt
  ROM #(.dataWidth(16)) rom_1 (.addr({8{1'b0}}), .data(ROW_ITERCOUNT));
  ROM #(.dataWidth(16)) rom_2 (.addr({8{1'b0}}), .data(COL_ITERCOUNT));

  // Notes on the sheet:
  //   Pipelined
  //   RAM A Addresses
  //   Constant High Bit
  //   RAM B Addresses
  //   Row[0]
  //   Row[1]
  //   A
  //   BY
  //   Col[0]
  //   Col[1]
  //   B
  //   AW
  //   S0
  //   S1
  //   S2
  //   S3
  //   O
  //   Control Unit
  //   contents of rom_1 (hex, n*v repeats v):
  //   1
  //   contents of rom_2 (hex, n*v repeats v):
  //   4
  //   Configuration RAM, Holds Matrix Size (N/4)[0], Data Type (0: int64, 1: float64)[1]
endmodule

module SUBCIRC_MatrixAdder (
  input  [63:0] B0,
  input  [63:0] A0,
  input  [63:0] B1,
  input  [63:0] A1,
  input  [63:0] B2,
  input  [63:0] A2,
  input  [63:0] B3,
  input  [63:0] A3,
  output [63:0] S0,
  output [63:0] S1,
  output [63:0] S2,
  output [63:0] S3
);

  Adder #(.width(64)) adder_1 (.a(B0), .b(A0), .out(S0));  // open: cin, cout
  Adder #(.width(64)) adder_2 (.a(B1), .b(A1), .out(S1));  // open: cin, cout
  Adder #(.width(64)) adder_3 (.a(B2), .b(A2), .out(S2));  // open: cin, cout
  Adder #(.width(64)) adder_4 (.a(B3), .b(A3), .out(S3));  // open: cin, cout

  // Notes on the sheet:
  //   Acts as a Addition Node
endmodule

module TEST_MatrixMultiplier (
);

  wire [63:0] subcirc_matrixadder_1_s0, subcirc_matrixadder_1_s1, subcirc_matrixadder_1_s2,
       subcirc_matrixadder_1_s3, subcirc_matrixmultiplier_1_s0, subcirc_matrixmultiplier_1_s1,
       subcirc_matrixmultiplier_1_s2, subcirc_matrixmultiplier_1_s3, subcirc_matrixmultiplier_1_w0,
       subcirc_matrixmultiplier_1_w1, subcirc_matrixmultiplier_1_w2, subcirc_matrixmultiplier_1_w3;

  SUBCIRC_MatrixMultiplier subcirc_matrixmultiplier_1 (
    .B0(64'h5), .A0(64'h1), .B1(64'h6), .A1(64'h2), .B2(64'h7), .A2(64'h3), .B3(64'h8), .A3(64'h4),
    .S0(subcirc_matrixmultiplier_1_s0), .S1(subcirc_matrixmultiplier_1_s1),
    .S2(subcirc_matrixmultiplier_1_s2), .S3(subcirc_matrixmultiplier_1_s3),
    .W0(subcirc_matrixmultiplier_1_w0), .W1(subcirc_matrixmultiplier_1_w1),
    .W2(subcirc_matrixmultiplier_1_w2), .W3(subcirc_matrixmultiplier_1_w3));
  SUBCIRC_MatrixAdder subcirc_matrixadder_1 (
    .B0(subcirc_matrixmultiplier_1_s0), .A0(subcirc_matrixmultiplier_1_w0),
    .B1(subcirc_matrixmultiplier_1_s1), .A1(subcirc_matrixmultiplier_1_w1),
    .B2(subcirc_matrixmultiplier_1_s2), .A2(subcirc_matrixmultiplier_1_w2),
    .B3(subcirc_matrixmultiplier_1_s3), .A3(subcirc_matrixmultiplier_1_w3), .S0(subcirc_matrixadder_1_s0),
    .S1(subcirc_matrixadder_1_s1), .S2(subcirc_matrixadder_1_s2), .S3(subcirc_matrixadder_1_s3));
  // Probe on subcirc_matrixadder_1_s0
  // Probe on subcirc_matrixadder_1_s2
  // Probe on subcirc_matrixadder_1_s1
  // Probe on subcirc_matrixadder_1_s3

  // Notes on the sheet:
  //   Subcircuit works perfectly for 2x2 Matrix Multiplicaton / Verified on multiple data with overflow
endmodule

module WorkBench (
);

  wire clock_1_out, clock_2_out;
  wire [7:0] counter_1_q, counter_2_q;
  wire [63:0] adder_1_out, adder_2_out, multiplier_1_out, multiplier_2_out, ram_1_dout, ram_2_dout,
       ram_3_dout, ram_4_dout, register_1_q, register_2_q;

  Clock clock_1 (.out(clock_1_out));
  RAM #(.dataWidth(64), .\type ("nonvolatile")) ram_1 (
    .addr(counter_1_q), .oe(1'b1), .clk(clock_1_out), .dout(ram_1_dout));  // open: we, din
  Counter counter_1 (.count(1'b1), .Q(counter_1_q), .up(1'b1), .clk(clock_1_out));  // open: load, D, carry, clr
  RAM #(.dataWidth(64), .\type ("nonvolatile")) ram_2 (
    .addr(counter_1_q), .oe(1'b1), .clk(clock_1_out), .dout(ram_2_dout));  // open: we, din
  Multiplier #(.width(64)) multiplier_1 (.a(ram_1_dout), .b(ram_2_dout), .out(multiplier_1_out));  // open: cin, cout
  Register #(.width(64)) register_1 (
    .D(multiplier_1_out), .en(1'b1), .Q(register_1_q), .clk(clock_1_out));  // open: clr
  Adder #(.width(64)) adder_1 (.a(register_1_q), .b(multiplier_1_out), .out(adder_1_out));  // open: cin, cout
  // Probe on adder_1_out
  Clock clock_2 (.out(clock_2_out));
  RAM #(.dataWidth(64), .\type ("nonvolatile")) ram_3 (
    .addr(counter_2_q), .oe(1'b1), .clk(clock_2_out), .dout(ram_3_dout));  // open: we, din
  Counter counter_2 (.count(1'b1), .Q(counter_2_q), .up(1'b1), .clk(clock_2_out));  // open: load, D, carry, clr
  RAM #(.dataWidth(64), .\type ("nonvolatile")) ram_4 (
    .addr(counter_2_q), .oe(1'b1), .clk(clock_2_out), .dout(ram_4_dout));  // open: we, din
  Multiplier #(.width(64)) multiplier_2 (.a(ram_3_dout), .b(ram_4_dout), .out(multiplier_2_out));  // open: cin, cout
  Register #(.width(64)) register_2 (
    .D(multiplier_2_out), .en(1'b1), .Q(register_2_q), .clk(clock_2_out));  // open: clr
  Adder #(.width(64)) adder_2 (.a(register_2_q), .b(multiplier_2_out), .out(adder_2_out));  // open: cin, cout
  // Probe on adder_2_out

  // Notes on the sheet:
  //   AB;CD
  //   A
  //   WX;YZ
  //   B
  //   AB;CD
  //   A
  //   WX;YZ
  //   B
endmodule

module RAMController (
  input  [7:0] rs,
  input  [7:0] rd,
  input  CLK,
  output [7:0] A,
  output WE,
  output OE
);

  D_Flip_Flop d_ff_1 (.clk(CLK), .D(1'b1), .Q(WE));  // open: Qn, preset, reset
  not not_1 (OE, CLK);
  Multiplexer #(.width(8)) multiplexer_1 (.in0(rs), .in1(rd), .out(A), .sel(CLK));
endmodule

module SUBCIRC_RAMBankOutput (
  input  [63:0] D3,
  input  [63:0] D2,
  input  [63:0] D1,
  input  [63:0] D0,
  input  [15:0] Address,
  input  WE,
  input  OE,
  input  CLK,
  output [63:0] S3,
  output [63:0] S2,
  output [63:0] S1,
  output [63:0] S0
);

  RAM #(.addrWidth(16), .dataWidth(64)) C1 (.addr(Address), .we(WE), .oe(OE), .clk(CLK), .din(D0), .dout(S0));
  RAM #(.addrWidth(16), .dataWidth(64)) ram_1 (.addr(Address), .we(WE), .oe(OE), .clk(CLK), .din(D1), .dout(S1));
  RAM #(.addrWidth(16), .dataWidth(64)) ram_2 (.addr(Address), .we(WE), .oe(OE), .clk(CLK), .din(D2), .dout(S2));
  RAM #(.addrWidth(16), .dataWidth(64)) ram_3 (.addr(Address), .we(WE), .oe(OE), .clk(CLK), .din(D3), .dout(S3));
endmodule

module TEST_Assebmly_ByDoc (
);

  wire CLOCK_GLOBAL;
  wire [7:0] RAM_A_ADDRESS, RAM_B_ADDRESS;
  wire [15:0] ITERCOUNT, RAM_S_ADDRESS, register_1_q, undriven;
  wire [63:0] subcirc_matrixadder_1_s0, subcirc_matrixadder_1_s1, subcirc_matrixadder_1_s2,
       subcirc_matrixadder_1_s3, subcirc_rambank_1_s0, subcirc_rambank_1_s1, subcirc_rambank_1_s2,
       subcirc_rambank_1_s3, subcirc_rambank_2_s0, subcirc_rambank_2_s1, subcirc_rambank_2_s2,
       subcirc_rambank_2_s3, subcirc_rambank_3_s0, subcirc_rambank_3_s1, subcirc_rambank_3_s2,
       subcirc_rambank_3_s3, subcirc_rambank_4_s0, subcirc_rambank_4_s1, subcirc_rambank_4_s2,
       subcirc_rambank_4_s3, test_core_1_s0, test_core_1_s1, test_core_1_s2, test_core_1_s3, undriven_2,
       undriven_3, undriven_4, undriven_5;

  Counter #(.max('hffff), .width(16)) counter_1 (
    .count(1'b1), .Q(RAM_S_ADDRESS), .up(1'b1), .clk(CLOCK_GLOBAL));  // open: load, D, carry, clr
  Counter counter_2 (.count(1'b1), .Q(RAM_A_ADDRESS), .up(1'b1), .clk(CLOCK_GLOBAL));  // open: load, D, carry, clr
  Comparator #(.mode("unsigned"), .width(16)) comparator_1 (.a(undriven), .b(RAM_S_ADDRESS));  // open: gt, eq, lt
  Counter counter_3 (.count(1'b1), .Q(RAM_B_ADDRESS), .up(1'b1), .clk(CLOCK_GLOBAL));  // open: load, D, carry, clr
  // Probe on RAM_B_ADDRESS
  // Probe on RAM_A_ADDRESS
  SUBCIRC_RAMBank subcirc_rambank_1 (
    .Address(RAM_A_ADDRESS), .OE(1'b1), .CLK(CLOCK_GLOBAL), .S3(subcirc_rambank_1_s3),
    .S2(subcirc_rambank_1_s2), .S1(subcirc_rambank_1_s1), .S0(subcirc_rambank_1_s0));  // open: D3, D2, D1, D0, WE
  SUBCIRC_RAMBank subcirc_rambank_2 (
    .Address(RAM_A_ADDRESS), .OE(1'b1), .CLK(CLOCK_GLOBAL), .S3(subcirc_rambank_2_s3),
    .S2(subcirc_rambank_2_s2), .S1(subcirc_rambank_2_s1), .S0(subcirc_rambank_2_s0));  // open: D3, D2, D1, D0, WE
  // Probe on subcirc_matrixadder_1_s3
  // Probe on subcirc_matrixadder_1_s1
  // Probe on test_core_1_s0
  // Probe on test_core_1_s2
  SUBCIRC_MatrixAdder subcirc_matrixadder_1 (
    .S0(subcirc_matrixadder_1_s0), .S1(subcirc_matrixadder_1_s1), .S2(subcirc_matrixadder_1_s2),
    .S3(subcirc_matrixadder_1_s3));  // open: B0, A0, B1, A1, B2, A2, B3, A3
  SUBCIRC_RAMBank subcirc_rambank_3 (
    .Address(RAM_B_ADDRESS), .OE(1'b1), .CLK(CLOCK_GLOBAL), .S3(subcirc_rambank_3_s3),
    .S2(subcirc_rambank_3_s2), .S1(subcirc_rambank_3_s1), .S0(subcirc_rambank_3_s0));  // open: D3, D2, D1, D0, WE
  SUBCIRC_RAMBank subcirc_rambank_4 (
    .Address(RAM_B_ADDRESS), .OE(1'b1), .CLK(CLOCK_GLOBAL), .S3(subcirc_rambank_4_s3),
    .S2(subcirc_rambank_4_s2), .S1(subcirc_rambank_4_s1), .S0(subcirc_rambank_4_s0));  // open: D3, D2, D1, D0, WE
  TEST_CORE test_core_1 (
    .B03(subcirc_rambank_3_s3), .B02(subcirc_rambank_3_s2), .B01(subcirc_rambank_3_s1),
    .B00(subcirc_rambank_3_s0), .B13(subcirc_rambank_4_s3), .B12(subcirc_rambank_4_s2),
    .B11(subcirc_rambank_4_s1), .B10(subcirc_rambank_4_s0), .A13(subcirc_rambank_2_s3),
    .A12(subcirc_rambank_2_s2), .A11(subcirc_rambank_2_s1), .A10(subcirc_rambank_2_s0),
    .A03(subcirc_rambank_1_s3), .A02(subcirc_rambank_1_s2), .A01(subcirc_rambank_1_s1),
    .A00(subcirc_rambank_1_s0), .S3(test_core_1_s3), .S2(test_core_1_s2), .S1(test_core_1_s1),
    .S0(test_core_1_s0));
  // Probe on subcirc_matrixadder_1_s2
  // Probe on subcirc_matrixadder_1_s0
  // Probe on test_core_1_s1
  // Probe on test_core_1_s3
  Register #(.width(16)) register_1 (.D(RAM_S_ADDRESS), .en(1'b1), .Q(register_1_q), .clk(CLOCK_GLOBAL));  // open: clr
  Clock clock_1 (.out(CLOCK_GLOBAL));
  SUBCIRC_RAMBankOutput subcirc_rambankoutput_1 (
    .D3(undriven_2), .D2(undriven_3), .D1(undriven_4), .D0(undriven_5), .Address(register_1_q),
    .CLK(CLOCK_GLOBAL));  // open: WE, OE, S3, S2, S1, S0
  ROM #(.dataWidth(16)) rom_1 (.addr({8{1'b0}}), .data(ITERCOUNT));

  // Notes on the sheet:
  //   Pipelined
  //   RAM A Addresses
  //   Constant High Bit
  //   RAM B Addresses
  //   Row[0]
  //   Row[1]
  //   A
  //   Col[0]
  //   Col[1]
  //   B
  //   O
  //   Configuration RAM, Holds Matrix Size (N/4)[0], Data Type (0: int64, 1: float64)[1]
endmodule

module TEST_SUBCIRC_MatrixMultiplier (
  input  [63:0] B3,
  input  [63:0] B2,
  input  [63:0] B1,
  input  [63:0] B0,
  input  [63:0] A3,
  input  [63:0] A2,
  input  [63:0] A1,
  input  [63:0] A0,
  output [63:0] S0,
  output [63:0] W0,
  output [63:0] S1,
  output [63:0] W1,
  output [63:0] S2,
  output [63:0] W2,
  output [63:0] S3,
  output [63:0] W3
);

  Multiplier #(.width(64)) multiplier_1 (.a(A0), .b(B0), .out(S0));  // open: cin, cout
  Multiplier #(.width(64)) multiplier_2 (.a(A0), .b(B1), .out(S1));  // open: cin, cout
  Multiplier #(.width(64)) multiplier_3 (.a(A2), .b(B0), .out(S2));  // open: cin, cout
  Multiplier #(.width(64)) multiplier_4 (.a(A2), .b(B1), .out(S3));  // open: cin, cout
  Multiplier #(.width(64)) multiplier_5 (.a(A1), .b(B2), .out(W0));  // open: cin, cout
  Multiplier #(.width(64)) multiplier_6 (.a(A1), .b(B3), .out(W1));  // open: cin, cout
  Multiplier #(.width(64)) multiplier_7 (.a(A3), .b(B2), .out(W2));  // open: cin, cout
  Multiplier #(.width(64)) multiplier_8 (.a(A3), .b(B3), .out(W3));  // open: cin, cout

  // Notes on the sheet:
  //   Acts as a Partial Multiplication Node
  //   Supports Partial Matrix Multiplication where A*B = S1, S2 where S = S1+S2
  //   A0B0
  //   A0B1
  //   A2B0
  //   A2B1
  //   A1B2
  //   A1B3
  //   A3B2
  //   A3B3
endmodule

module TEST_CORE (
  input  [63:0] B03,
  input  [63:0] B02,
  input  [63:0] B01,
  input  [63:0] B00,
  input  [63:0] B13,
  input  [63:0] B12,
  input  [63:0] B11,
  input  [63:0] B10,
  input  [63:0] A13,
  input  [63:0] A12,
  input  [63:0] A11,
  input  [63:0] A10,
  input  [63:0] A03,
  input  [63:0] A02,
  input  [63:0] A01,
  input  [63:0] A00,
  output [63:0] S3,
  output [63:0] S2,
  output [63:0] S1,
  output [63:0] S0
);

  wire [63:0] subcirc_matrixadder_1_s0, subcirc_matrixadder_1_s1, subcirc_matrixadder_1_s2,
       subcirc_matrixadder_1_s3, subcirc_matrixadder_2_s0, subcirc_matrixadder_2_s1,
       subcirc_matrixadder_2_s2, subcirc_matrixadder_2_s3, test_subcirc_matrixmultiplier_1_s0,
       test_subcirc_matrixmultiplier_1_s1, test_subcirc_matrixmultiplier_1_s2,
       test_subcirc_matrixmultiplier_1_s3, test_subcirc_matrixmultiplier_1_w0,
       test_subcirc_matrixmultiplier_1_w1, test_subcirc_matrixmultiplier_1_w2,
       test_subcirc_matrixmultiplier_1_w3, test_subcirc_matrixmultiplier_2_s0,
       test_subcirc_matrixmultiplier_2_s1, test_subcirc_matrixmultiplier_2_s2,
       test_subcirc_matrixmultiplier_2_s3, test_subcirc_matrixmultiplier_2_w0,
       test_subcirc_matrixmultiplier_2_w1, test_subcirc_matrixmultiplier_2_w2,
       test_subcirc_matrixmultiplier_2_w3;

  TEST_SUBCIRC_MatrixMultiplier test_subcirc_matrixmultiplier_1 (
    .B3(B13), .B2(B12), .B1(B11), .B0(B10), .A3(A13), .A2(A12), .A1(A11), .A0(A10),
    .S0(test_subcirc_matrixmultiplier_1_s0), .W0(test_subcirc_matrixmultiplier_1_w0),
    .S1(test_subcirc_matrixmultiplier_1_s1), .W1(test_subcirc_matrixmultiplier_1_w1),
    .S2(test_subcirc_matrixmultiplier_1_s2), .W2(test_subcirc_matrixmultiplier_1_w2),
    .S3(test_subcirc_matrixmultiplier_1_s3), .W3(test_subcirc_matrixmultiplier_1_w3));
  SUBCIRC_MatrixAdder subcirc_matrixadder_1 (
    .B0(test_subcirc_matrixmultiplier_1_s0), .A0(test_subcirc_matrixmultiplier_1_w0),
    .B1(test_subcirc_matrixmultiplier_1_s1), .A1(test_subcirc_matrixmultiplier_1_w1),
    .B2(test_subcirc_matrixmultiplier_1_s2), .A2(test_subcirc_matrixmultiplier_1_w2),
    .B3(test_subcirc_matrixmultiplier_1_s3), .A3(test_subcirc_matrixmultiplier_1_w3),
    .S0(subcirc_matrixadder_1_s0), .S1(subcirc_matrixadder_1_s1), .S2(subcirc_matrixadder_1_s2),
    .S3(subcirc_matrixadder_1_s3));
  TEST_SUBCIRC_MatrixMultiplier test_subcirc_matrixmultiplier_2 (
    .B3(B03), .B2(B02), .B1(B01), .B0(B00), .A3(A03), .A2(A02), .A1(A01), .A0(A00),
    .S0(test_subcirc_matrixmultiplier_2_s0), .W0(test_subcirc_matrixmultiplier_2_w0),
    .S1(test_subcirc_matrixmultiplier_2_s1), .W1(test_subcirc_matrixmultiplier_2_w1),
    .S2(test_subcirc_matrixmultiplier_2_s2), .W2(test_subcirc_matrixmultiplier_2_w2),
    .S3(test_subcirc_matrixmultiplier_2_s3), .W3(test_subcirc_matrixmultiplier_2_w3));
  SUBCIRC_MatrixAdder subcirc_matrixadder_2 (
    .B0(test_subcirc_matrixmultiplier_2_s0), .A0(test_subcirc_matrixmultiplier_2_w0),
    .B1(test_subcirc_matrixmultiplier_2_s1), .A1(test_subcirc_matrixmultiplier_2_w1),
    .B2(test_subcirc_matrixmultiplier_2_s2), .A2(test_subcirc_matrixmultiplier_2_w2),
    .B3(test_subcirc_matrixmultiplier_2_s3), .A3(test_subcirc_matrixmultiplier_2_w3),
    .S0(subcirc_matrixadder_2_s0), .S1(subcirc_matrixadder_2_s1), .S2(subcirc_matrixadder_2_s2),
    .S3(subcirc_matrixadder_2_s3));
  SUBCIRC_MatrixAdder subcirc_matrixadder_3 (
    .B0(subcirc_matrixadder_2_s0), .A0(subcirc_matrixadder_1_s0), .B1(subcirc_matrixadder_2_s1),
    .A1(subcirc_matrixadder_1_s1), .B2(subcirc_matrixadder_2_s2), .A2(subcirc_matrixadder_1_s2),
    .B3(subcirc_matrixadder_2_s3), .A3(subcirc_matrixadder_1_s3), .S0(S3), .S1(S2), .S2(S1), .S3(S0));

  // Notes on the sheet:
  //   by
  //   aw
endmodule

module TEST_SUBCIRC_MatrixAdder (
  input  [63:0] B0,
  input  [63:0] B1,
  input  [63:0] B2,
  input  [63:0] B3,
  input  [63:0] A0,
  input  [63:0] A1,
  input  [63:0] A2,
  input  [63:0] A3,
  output [63:0] S0,
  output [63:0] S1,
  output [63:0] S2,
  output [63:0] S3
);

  Adder #(.width(64)) adder_1 (.a(B0), .b(A0), .out(S0));  // open: cin, cout
  Adder #(.width(64)) adder_2 (.a(B1), .b(A1), .out(S1));  // open: cin, cout
  Adder #(.width(64)) adder_3 (.a(B2), .b(A2), .out(S2));  // open: cin, cout
  Adder #(.width(64)) adder_4 (.a(B3), .b(A3), .out(S3));  // open: cin, cout

  // Notes on the sheet:
  //   Acts as a Addition Node
endmodule

module Quiz (
);

  wire CLOCK_GLOBAL, comparator_1_eq, comparator_2_eq;
  wire [7:0] counter_4_q, counter_5_q, RAM_A_ADDRESS, RAM_B_ADDRESS;
  wire [15:0] bit_extender_1_out, bit_extender_2_out, COL_ITERCOUNT, RAM_S_ADDRESS, register_1_q,
       ROW_ITERCOUNT;
  wire [63:0] S0, S1, S2, S3, subcirc_matrixadder_1_s0, subcirc_matrixadder_1_s1, subcirc_matrixadder_1_s2,
       subcirc_matrixadder_1_s3, subcirc_matrixadder_2_s0, subcirc_matrixadder_2_s1,
       subcirc_matrixadder_2_s2, subcirc_matrixadder_2_s3, subcirc_matrixadder_3_s0,
       subcirc_matrixadder_3_s1, subcirc_matrixadder_3_s2, subcirc_matrixadder_3_s3,
       subcirc_matrixadder_4_s0, subcirc_matrixadder_4_s1, subcirc_matrixadder_4_s2,
       subcirc_matrixadder_4_s3, subcirc_matrixadder_5_s0, subcirc_matrixadder_5_s1,
       subcirc_matrixadder_5_s2, subcirc_matrixadder_5_s3, subcirc_rambank_1_s0, subcirc_rambank_1_s1,
       subcirc_rambank_1_s2, subcirc_rambank_1_s3, subcirc_rambank_2_s0, subcirc_rambank_2_s1,
       subcirc_rambank_2_s2, subcirc_rambank_2_s3, subcirc_rambank_3_s0, subcirc_rambank_3_s1,
       subcirc_rambank_3_s2, subcirc_rambank_3_s3, subcirc_rambank_4_s0, subcirc_rambank_4_s1,
       subcirc_rambank_4_s2, subcirc_rambank_4_s3, subcirc_rambank_5_s0, subcirc_rambank_5_s1,
       subcirc_rambank_5_s2, subcirc_rambank_5_s3, subcirc_rambank_6_s0, subcirc_rambank_6_s1,
       subcirc_rambank_6_s2, subcirc_rambank_6_s3, subcirc_rambank_7_s0, subcirc_rambank_7_s1,
       subcirc_rambank_7_s2, subcirc_rambank_7_s3, subcirc_rambank_8_s0, subcirc_rambank_8_s1,
       subcirc_rambank_8_s2, subcirc_rambank_8_s3, subcirc_rambankoutput_1_s0, subcirc_rambankoutput_1_s1,
       subcirc_rambankoutput_1_s2, subcirc_rambankoutput_1_s3, test_subcirc_matrixadder_1_s0,
       test_subcirc_matrixadder_1_s1, test_subcirc_matrixadder_1_s2, test_subcirc_matrixadder_1_s3,
       test_subcirc_matrixadder_2_s0, test_subcirc_matrixadder_2_s1, test_subcirc_matrixadder_2_s2,
       test_subcirc_matrixadder_2_s3, test_subcirc_matrixmultiplier_1_s0, test_subcirc_matrixmultiplier_1_s1,
       test_subcirc_matrixmultiplier_1_s2, test_subcirc_matrixmultiplier_1_s3,
       test_subcirc_matrixmultiplier_1_w0, test_subcirc_matrixmultiplier_1_w1,
       test_subcirc_matrixmultiplier_1_w2, test_subcirc_matrixmultiplier_1_w3,
       test_subcirc_matrixmultiplier_2_s0, test_subcirc_matrixmultiplier_2_s1,
       test_subcirc_matrixmultiplier_2_s2, test_subcirc_matrixmultiplier_2_s3,
       test_subcirc_matrixmultiplier_2_w0, test_subcirc_matrixmultiplier_2_w1,
       test_subcirc_matrixmultiplier_2_w2, test_subcirc_matrixmultiplier_2_w3,
       test_subcirc_matrixmultiplier_3_s0, test_subcirc_matrixmultiplier_3_s1,
       test_subcirc_matrixmultiplier_3_s2, test_subcirc_matrixmultiplier_3_s3,
       test_subcirc_matrixmultiplier_3_w0, test_subcirc_matrixmultiplier_3_w1,
       test_subcirc_matrixmultiplier_3_w2, test_subcirc_matrixmultiplier_3_w3,
       test_subcirc_matrixmultiplier_4_s0, test_subcirc_matrixmultiplier_4_s1,
       test_subcirc_matrixmultiplier_4_s2, test_subcirc_matrixmultiplier_4_s3,
       test_subcirc_matrixmultiplier_4_w0, test_subcirc_matrixmultiplier_4_w1,
       test_subcirc_matrixmultiplier_4_w2, test_subcirc_matrixmultiplier_4_w3;

  Counter #(.max('hffff), .width(16)) counter_1 (
    .count(1'b1), .Q(RAM_S_ADDRESS), .up(1'b1), .clk(CLOCK_GLOBAL));  // open: load, D, carry, clr
  Counter counter_2 (.count(1'b1), .Q(RAM_A_ADDRESS), .up(1'b1), .clk(CLOCK_GLOBAL));  // open: load, D, carry, clr
  Counter counter_3 (.count(1'b1), .Q(RAM_B_ADDRESS), .up(1'b1), .clk(CLOCK_GLOBAL));  // open: load, D, carry, clr
  // Probe on RAM_B_ADDRESS
  // Probe on RAM_A_ADDRESS
  SUBCIRC_RAMBank subcirc_rambank_1 (
    .Address(RAM_A_ADDRESS), .OE(1'b1), .CLK(CLOCK_GLOBAL), .S3(subcirc_rambank_1_s3),
    .S2(subcirc_rambank_1_s2), .S1(subcirc_rambank_1_s1), .S0(subcirc_rambank_1_s0));  // open: D3, D2, D1, D0, WE
  SUBCIRC_RAMBank subcirc_rambank_2 (
    .Address(RAM_A_ADDRESS), .OE(1'b1), .CLK(CLOCK_GLOBAL), .S3(subcirc_rambank_2_s3),
    .S2(subcirc_rambank_2_s2), .S1(subcirc_rambank_2_s1), .S0(subcirc_rambank_2_s0));  // open: D3, D2, D1, D0, WE
  SUBCIRC_RAMBank subcirc_rambank_3 (
    .Address(RAM_A_ADDRESS), .OE(1'b1), .CLK(CLOCK_GLOBAL), .S3(subcirc_rambank_3_s3),
    .S2(subcirc_rambank_3_s2), .S1(subcirc_rambank_3_s1), .S0(subcirc_rambank_3_s0));  // open: D3, D2, D1, D0, WE
  SUBCIRC_RAMBank subcirc_rambank_4 (
    .Address(RAM_A_ADDRESS), .OE(1'b1), .CLK(CLOCK_GLOBAL), .S3(subcirc_rambank_4_s3),
    .S2(subcirc_rambank_4_s2), .S1(subcirc_rambank_4_s1), .S0(subcirc_rambank_4_s0));  // open: D3, D2, D1, D0, WE
  // Probe on subcirc_matrixadder_1_s3
  // Probe on subcirc_matrixadder_1_s1
  SUBCIRC_MatrixAdder subcirc_matrixadder_1 (
    .S0(subcirc_matrixadder_1_s0), .S1(subcirc_matrixadder_1_s1), .S2(subcirc_matrixadder_1_s2),
    .S3(subcirc_matrixadder_1_s3));  // open: B0, A0, B1, A1, B2, A2, B3, A3
  SUBCIRC_RAMBank subcirc_rambank_5 (
    .Address(RAM_B_ADDRESS), .OE(1'b1), .CLK(CLOCK_GLOBAL), .S3(subcirc_rambank_5_s3),
    .S2(subcirc_rambank_5_s2), .S1(subcirc_rambank_5_s1), .S0(subcirc_rambank_5_s0));  // open: D3, D2, D1, D0, WE
  SUBCIRC_RAMBank subcirc_rambank_6 (
    .Address(RAM_B_ADDRESS), .OE(1'b1), .CLK(CLOCK_GLOBAL), .S3(subcirc_rambank_6_s3),
    .S2(subcirc_rambank_6_s2), .S1(subcirc_rambank_6_s1), .S0(subcirc_rambank_6_s0));  // open: D3, D2, D1, D0, WE
  SUBCIRC_RAMBank subcirc_rambank_7 (
    .Address(RAM_B_ADDRESS), .OE(1'b1), .CLK(CLOCK_GLOBAL), .S3(subcirc_rambank_7_s3),
    .S2(subcirc_rambank_7_s2), .S1(subcirc_rambank_7_s1), .S0(subcirc_rambank_7_s0));  // open: D3, D2, D1, D0, WE
  SUBCIRC_RAMBank subcirc_rambank_8 (
    .Address(RAM_B_ADDRESS), .OE(1'b1), .CLK(CLOCK_GLOBAL), .S3(subcirc_rambank_8_s3),
    .S2(subcirc_rambank_8_s2), .S1(subcirc_rambank_8_s1), .S0(subcirc_rambank_8_s0));  // open: D3, D2, D1, D0, WE
  // Probe on subcirc_matrixadder_1_s2
  // Probe on subcirc_matrixadder_1_s0
  Register #(.width(16)) register_1 (.D(RAM_S_ADDRESS), .en(1'b1), .Q(register_1_q), .clk(CLOCK_GLOBAL));  // open: clr
  TEST_SUBCIRC_MatrixMultiplier test_subcirc_matrixmultiplier_1 (
    .B3(subcirc_rambank_5_s3), .B2(subcirc_rambank_5_s2), .B1(subcirc_rambank_5_s1),
    .B0(subcirc_rambank_5_s0), .A3(subcirc_rambank_1_s3), .A2(subcirc_rambank_1_s2),
    .A1(subcirc_rambank_1_s1), .A0(subcirc_rambank_1_s0), .S0(test_subcirc_matrixmultiplier_1_s0),
    .W0(test_subcirc_matrixmultiplier_1_w0), .S1(test_subcirc_matrixmultiplier_1_s1),
    .W1(test_subcirc_matrixmultiplier_1_w1), .S2(test_subcirc_matrixmultiplier_1_s2),
    .W2(test_subcirc_matrixmultiplier_1_w2), .S3(test_subcirc_matrixmultiplier_1_s3),
    .W3(test_subcirc_matrixmultiplier_1_w3));
  SUBCIRC_MatrixAdder subcirc_matrixadder_2 (
    .B0(test_subcirc_matrixmultiplier_1_s0), .A0(test_subcirc_matrixmultiplier_1_w0),
    .B1(test_subcirc_matrixmultiplier_1_s1), .A1(test_subcirc_matrixmultiplier_1_w1),
    .B2(test_subcirc_matrixmultiplier_1_s2), .A2(test_subcirc_matrixmultiplier_1_w2),
    .B3(test_subcirc_matrixmultiplier_1_s3), .A3(test_subcirc_matrixmultiplier_1_w3),
    .S0(subcirc_matrixadder_2_s0), .S1(subcirc_matrixadder_2_s1), .S2(subcirc_matrixadder_2_s2),
    .S3(subcirc_matrixadder_2_s3));
  TEST_SUBCIRC_MatrixMultiplier test_subcirc_matrixmultiplier_2 (
    .B3(subcirc_rambank_6_s3), .B2(subcirc_rambank_6_s2), .B1(subcirc_rambank_6_s1),
    .B0(subcirc_rambank_6_s0), .A3(subcirc_rambank_2_s3), .A2(subcirc_rambank_2_s2),
    .A1(subcirc_rambank_2_s1), .A0(subcirc_rambank_2_s0), .S0(test_subcirc_matrixmultiplier_2_s0),
    .W0(test_subcirc_matrixmultiplier_2_w0), .S1(test_subcirc_matrixmultiplier_2_s1),
    .W1(test_subcirc_matrixmultiplier_2_w1), .S2(test_subcirc_matrixmultiplier_2_s2),
    .W2(test_subcirc_matrixmultiplier_2_w2), .S3(test_subcirc_matrixmultiplier_2_s3),
    .W3(test_subcirc_matrixmultiplier_2_w3));
  SUBCIRC_MatrixAdder subcirc_matrixadder_3 (
    .B0(test_subcirc_matrixmultiplier_2_s0), .A0(test_subcirc_matrixmultiplier_2_w0),
    .B1(test_subcirc_matrixmultiplier_2_s1), .A1(test_subcirc_matrixmultiplier_2_w1),
    .B2(test_subcirc_matrixmultiplier_2_s2), .A2(test_subcirc_matrixmultiplier_2_w2),
    .B3(test_subcirc_matrixmultiplier_2_s3), .A3(test_subcirc_matrixmultiplier_2_w3),
    .S0(subcirc_matrixadder_3_s0), .S1(subcirc_matrixadder_3_s1), .S2(subcirc_matrixadder_3_s2),
    .S3(subcirc_matrixadder_3_s3));
  TEST_SUBCIRC_MatrixMultiplier test_subcirc_matrixmultiplier_3 (
    .B3(subcirc_rambank_7_s3), .B2(subcirc_rambank_7_s2), .B1(subcirc_rambank_7_s1),
    .B0(subcirc_rambank_7_s0), .A3(subcirc_rambank_3_s3), .A2(subcirc_rambank_3_s2),
    .A1(subcirc_rambank_3_s1), .A0(subcirc_rambank_3_s0), .S0(test_subcirc_matrixmultiplier_3_s0),
    .W0(test_subcirc_matrixmultiplier_3_w0), .S1(test_subcirc_matrixmultiplier_3_s1),
    .W1(test_subcirc_matrixmultiplier_3_w1), .S2(test_subcirc_matrixmultiplier_3_s2),
    .W2(test_subcirc_matrixmultiplier_3_w2), .S3(test_subcirc_matrixmultiplier_3_s3),
    .W3(test_subcirc_matrixmultiplier_3_w3));
  SUBCIRC_MatrixAdder subcirc_matrixadder_4 (
    .B0(test_subcirc_matrixmultiplier_3_s0), .A0(test_subcirc_matrixmultiplier_3_w0),
    .B1(test_subcirc_matrixmultiplier_3_s1), .A1(test_subcirc_matrixmultiplier_3_w1),
    .B2(test_subcirc_matrixmultiplier_3_s2), .A2(test_subcirc_matrixmultiplier_3_w2),
    .B3(test_subcirc_matrixmultiplier_3_s3), .A3(test_subcirc_matrixmultiplier_3_w3),
    .S0(subcirc_matrixadder_4_s0), .S1(subcirc_matrixadder_4_s1), .S2(subcirc_matrixadder_4_s2),
    .S3(subcirc_matrixadder_4_s3));
  TEST_SUBCIRC_MatrixMultiplier test_subcirc_matrixmultiplier_4 (
    .B3(subcirc_rambank_8_s3), .B2(subcirc_rambank_8_s2), .B1(subcirc_rambank_8_s1),
    .B0(subcirc_rambank_8_s0), .A3(subcirc_rambank_4_s3), .A2(subcirc_rambank_4_s2),
    .A1(subcirc_rambank_4_s1), .A0(subcirc_rambank_4_s0), .S0(test_subcirc_matrixmultiplier_4_s0),
    .W0(test_subcirc_matrixmultiplier_4_w0), .S1(test_subcirc_matrixmultiplier_4_s1),
    .W1(test_subcirc_matrixmultiplier_4_w1), .S2(test_subcirc_matrixmultiplier_4_s2),
    .W2(test_subcirc_matrixmultiplier_4_w2), .S3(test_subcirc_matrixmultiplier_4_s3),
    .W3(test_subcirc_matrixmultiplier_4_w3));
  SUBCIRC_MatrixAdder subcirc_matrixadder_5 (
    .B0(test_subcirc_matrixmultiplier_4_s0), .A0(test_subcirc_matrixmultiplier_4_w0),
    .B1(test_subcirc_matrixmultiplier_4_s1), .A1(test_subcirc_matrixmultiplier_4_w1),
    .B2(test_subcirc_matrixmultiplier_4_s2), .A2(test_subcirc_matrixmultiplier_4_w2),
    .B3(test_subcirc_matrixmultiplier_4_s3), .A3(test_subcirc_matrixmultiplier_4_w3),
    .S0(subcirc_matrixadder_5_s0), .S1(subcirc_matrixadder_5_s1), .S2(subcirc_matrixadder_5_s2),
    .S3(subcirc_matrixadder_5_s3));
  Clock clock_1 (.out(CLOCK_GLOBAL));
  TEST_SUBCIRC_MatrixAdder test_subcirc_matrixadder_1 (
    .B0(subcirc_matrixadder_2_s0), .B1(subcirc_matrixadder_2_s1), .B2(subcirc_matrixadder_2_s2),
    .B3(subcirc_matrixadder_2_s3), .A0(subcirc_matrixadder_3_s0), .A1(subcirc_matrixadder_3_s1),
    .A2(subcirc_matrixadder_3_s2), .A3(subcirc_matrixadder_3_s3), .S0(test_subcirc_matrixadder_1_s0),
    .S1(test_subcirc_matrixadder_1_s1), .S2(test_subcirc_matrixadder_1_s2), .S3(test_subcirc_matrixadder_1_s3));
  TEST_SUBCIRC_MatrixAdder test_subcirc_matrixadder_2 (
    .B0(subcirc_matrixadder_4_s0), .B1(subcirc_matrixadder_4_s1), .B2(subcirc_matrixadder_4_s2),
    .B3(subcirc_matrixadder_4_s3), .A0(subcirc_matrixadder_5_s0), .A1(subcirc_matrixadder_5_s1),
    .A2(subcirc_matrixadder_5_s2), .A3(subcirc_matrixadder_5_s3), .S0(test_subcirc_matrixadder_2_s0),
    .S1(test_subcirc_matrixadder_2_s1), .S2(test_subcirc_matrixadder_2_s2), .S3(test_subcirc_matrixadder_2_s3));
  // Probe on subcirc_matrixadder_2_s0
  TEST_SUBCIRC_MatrixAdder test_subcirc_matrixadder_3 (
    .B0(test_subcirc_matrixadder_1_s0), .B1(test_subcirc_matrixadder_1_s1),
    .B2(test_subcirc_matrixadder_1_s2), .B3(test_subcirc_matrixadder_1_s3),
    .A0(test_subcirc_matrixadder_2_s0), .A1(test_subcirc_matrixadder_2_s1),
    .A2(test_subcirc_matrixadder_2_s2), .A3(test_subcirc_matrixadder_2_s3), .S0(S0), .S1(S1), .S2(S2), .S3(S3));
  SUBCIRC_RAMBankOutput subcirc_rambankoutput_1 (
    .D3(S3), .D2(S2), .D1(S1), .D0(S0), .Address(register_1_q), .WE(1'b1), .CLK(CLOCK_GLOBAL),
    .S3(subcirc_rambankoutput_1_s3), .S2(subcirc_rambankoutput_1_s2), .S1(subcirc_rambankoutput_1_s1),
    .S0(subcirc_rambankoutput_1_s0));  // open: OE
  // Probe on S0
  // Probe on S2
  // Probe on S1
  // Probe on S3
  assign bit_extender_1_out = {{8{counter_4_q[7]}}, counter_4_q};  // Bit_Extender bit_extender_1
  Counter counter_4 (.Q(counter_4_q));  // open: load, D, count, carry, up, clk, clr
  assign bit_extender_2_out = {{8{counter_5_q[7]}}, counter_5_q};  // Bit_Extender bit_extender_2
  Counter counter_5 (.Q(counter_5_q));  // open: load, D, count, carry, up, clk, clr
  Comparator #(.width(16)) comparator_1 (
    .a(bit_extender_1_out), .b(ROW_ITERCOUNT), .eq(comparator_1_eq));  // open: gt, lt
  Comparator #(.width(16)) comparator_2 (
    .a(bit_extender_2_out), .b(COL_ITERCOUNT), .eq(comparator_2_eq));  // open: gt, lt
  ROM #(.dataWidth(16)) rom_1 (.addr({8{1'b0}}), .data(ROW_ITERCOUNT));
  ROM #(.dataWidth(16)) rom_2 (.addr({8{1'b0}}), .data(COL_ITERCOUNT));

  // Notes on the sheet:
  //   Pipelined
  //   RAM A Addresses
  //   Constant High Bit
  //   RAM B Addresses
  //   Row[0][0]
  //   Row[0][1]
  //   Row[0][2]
  //   Row[0][3]
  //   A
  //   A
  //   Col[0][0]
  //   Col[0][1]
  //   Col[0][2]
  //   Col[0][3]
  //   B
  //   B
  //   AW
  //   BY
  //   O
  //   Control Unit
  //   contents of rom_1 (hex, n*v repeats v):
  //   1
  //   contents of rom_2 (hex, n*v repeats v):
  //   4
  //   Configuration RAM, Holds Matrix Size (N/4)[0], Data Type (0: int64, 1: float64)[1]
endmodule

module QuizV2 (
);

  wire CLOCK_GLOBAL, comparator_1_eq, comparator_2_eq, counter_3_carry;
  wire [7:0] counter_2_q, counter_3_q, counter_4_q, counter_5_q, multiplexer_1_out, multiplexer_2_out,
       RAM_A_ADDRESS, RAM_B_ADDRESS;
  wire [15:0] bit_extender_1_out, bit_extender_2_out, COL_ITERCOUNT, RAM_S_ADDRESS, register_1_q,
       ROW_ITERCOUNT;
  wire [63:0] S0, S1, S2, S3, subcirc_matrixadder_1_s0, subcirc_matrixadder_1_s1, subcirc_matrixadder_1_s2,
       subcirc_matrixadder_1_s3, subcirc_matrixadder_2_s0, subcirc_matrixadder_2_s1,
       subcirc_matrixadder_2_s2, subcirc_matrixadder_2_s3, subcirc_matrixadder_3_s0,
       subcirc_matrixadder_3_s1, subcirc_matrixadder_3_s2, subcirc_matrixadder_3_s3,
       subcirc_matrixadder_4_s0, subcirc_matrixadder_4_s1, subcirc_matrixadder_4_s2,
       subcirc_matrixadder_4_s3, subcirc_matrixadder_5_s0, subcirc_matrixadder_5_s1,
       subcirc_matrixadder_5_s2, subcirc_matrixadder_5_s3, subcirc_rambank_1_s0, subcirc_rambank_1_s1,
       subcirc_rambank_1_s2, subcirc_rambank_1_s3, subcirc_rambank_2_s0, subcirc_rambank_2_s1,
       subcirc_rambank_2_s2, subcirc_rambank_2_s3, subcirc_rambank_3_s0, subcirc_rambank_3_s1,
       subcirc_rambank_3_s2, subcirc_rambank_3_s3, subcirc_rambank_4_s0, subcirc_rambank_4_s1,
       subcirc_rambank_4_s2, subcirc_rambank_4_s3, subcirc_rambank_5_s0, subcirc_rambank_5_s1,
       subcirc_rambank_5_s2, subcirc_rambank_5_s3, subcirc_rambank_6_s0, subcirc_rambank_6_s1,
       subcirc_rambank_6_s2, subcirc_rambank_6_s3, subcirc_rambank_7_s0, subcirc_rambank_7_s1,
       subcirc_rambank_7_s2, subcirc_rambank_7_s3, subcirc_rambank_8_s0, subcirc_rambank_8_s1,
       subcirc_rambank_8_s2, subcirc_rambank_8_s3, subcirc_rambankoutput_1_s0, subcirc_rambankoutput_1_s1,
       subcirc_rambankoutput_1_s2, subcirc_rambankoutput_1_s3, test_subcirc_matrixadder_1_s0,
       test_subcirc_matrixadder_1_s1, test_subcirc_matrixadder_1_s2, test_subcirc_matrixadder_1_s3,
       test_subcirc_matrixadder_2_s0, test_subcirc_matrixadder_2_s1, test_subcirc_matrixadder_2_s2,
       test_subcirc_matrixadder_2_s3, test_subcirc_matrixmultiplier_1_s0, test_subcirc_matrixmultiplier_1_s1,
       test_subcirc_matrixmultiplier_1_s2, test_subcirc_matrixmultiplier_1_s3,
       test_subcirc_matrixmultiplier_1_w0, test_subcirc_matrixmultiplier_1_w1,
       test_subcirc_matrixmultiplier_1_w2, test_subcirc_matrixmultiplier_1_w3,
       test_subcirc_matrixmultiplier_2_s0, test_subcirc_matrixmultiplier_2_s1,
       test_subcirc_matrixmultiplier_2_s2, test_subcirc_matrixmultiplier_2_s3,
       test_subcirc_matrixmultiplier_2_w0, test_subcirc_matrixmultiplier_2_w1,
       test_subcirc_matrixmultiplier_2_w2, test_subcirc_matrixmultiplier_2_w3,
       test_subcirc_matrixmultiplier_3_s0, test_subcirc_matrixmultiplier_3_s1,
       test_subcirc_matrixmultiplier_3_s2, test_subcirc_matrixmultiplier_3_s3,
       test_subcirc_matrixmultiplier_3_w0, test_subcirc_matrixmultiplier_3_w1,
       test_subcirc_matrixmultiplier_3_w2, test_subcirc_matrixmultiplier_3_w3,
       test_subcirc_matrixmultiplier_4_s0, test_subcirc_matrixmultiplier_4_s1,
       test_subcirc_matrixmultiplier_4_s2, test_subcirc_matrixmultiplier_4_s3,
       test_subcirc_matrixmultiplier_4_w0, test_subcirc_matrixmultiplier_4_w1,
       test_subcirc_matrixmultiplier_4_w2, test_subcirc_matrixmultiplier_4_w3;

  Counter #(.max('hffff), .width(16)) counter_1 (
    .count(1'b1), .Q(RAM_S_ADDRESS), .up(1'b1), .clk(CLOCK_GLOBAL));  // open: load, D, carry, clr
  Counter #(.max('h1)) counter_2 (
    .count(counter_3_carry), .Q(counter_2_q), .up(1'b1), .clk(CLOCK_GLOBAL));  // open: load, D, carry, clr
  Multiplexer #(.width(8)) multiplexer_1 (.in0(8'h4), .in1({8{1'b0}}), .out(multiplexer_1_out));  // open: sel
  Multiplexer #(.width(8)) multiplexer_2 (.in0(8'h4), .in1({8{1'b0}}), .out(multiplexer_2_out));  // open: sel
  Counter #(.max('h1)) counter_3 (
    .count(1'b1), .Q(counter_3_q), .carry(counter_3_carry), .up(1'b1), .clk(CLOCK_GLOBAL));  // open: load, D, clr
  Adder adder_1 (.a(multiplexer_1_out), .b(counter_2_q), .out(RAM_A_ADDRESS));  // open: cin, cout
  Adder adder_2 (.a(multiplexer_2_out), .b(counter_3_q), .out(RAM_B_ADDRESS));  // open: cin, cout
  // Probe on counter_3_q
  // Probe on counter_2_q
  SUBCIRC_RAMBank subcirc_rambank_1 (
    .Address(RAM_A_ADDRESS), .OE(1'b1), .CLK(CLOCK_GLOBAL), .S3(subcirc_rambank_1_s3),
    .S2(subcirc_rambank_1_s2), .S1(subcirc_rambank_1_s1), .S0(subcirc_rambank_1_s0));  // open: D3, D2, D1, D0, WE
  SUBCIRC_RAMBank subcirc_rambank_2 (
    .Address(RAM_A_ADDRESS), .OE(1'b1), .CLK(CLOCK_GLOBAL), .S3(subcirc_rambank_2_s3),
    .S2(subcirc_rambank_2_s2), .S1(subcirc_rambank_2_s1), .S0(subcirc_rambank_2_s0));  // open: D3, D2, D1, D0, WE
  SUBCIRC_RAMBank subcirc_rambank_3 (
    .Address(RAM_A_ADDRESS), .OE(1'b1), .CLK(CLOCK_GLOBAL), .S3(subcirc_rambank_3_s3),
    .S2(subcirc_rambank_3_s2), .S1(subcirc_rambank_3_s1), .S0(subcirc_rambank_3_s0));  // open: D3, D2, D1, D0, WE
  SUBCIRC_RAMBank subcirc_rambank_4 (
    .Address(RAM_A_ADDRESS), .OE(1'b1), .CLK(CLOCK_GLOBAL), .S3(subcirc_rambank_4_s3),
    .S2(subcirc_rambank_4_s2), .S1(subcirc_rambank_4_s1), .S0(subcirc_rambank_4_s0));  // open: D3, D2, D1, D0, WE
  // Probe on subcirc_matrixadder_1_s3
  // Probe on subcirc_matrixadder_1_s1
  // Probe on subcirc_rambank_2_s0
  SUBCIRC_MatrixAdder subcirc_matrixadder_1 (
    .S0(subcirc_matrixadder_1_s0), .S1(subcirc_matrixadder_1_s1), .S2(subcirc_matrixadder_1_s2),
    .S3(subcirc_matrixadder_1_s3));  // open: B0, A0, B1, A1, B2, A2, B3, A3
  SUBCIRC_RAMBank subcirc_rambank_5 (
    .Address(RAM_B_ADDRESS), .OE(1'b1), .CLK(CLOCK_GLOBAL), .S3(subcirc_rambank_5_s3),
    .S2(subcirc_rambank_5_s2), .S1(subcirc_rambank_5_s1), .S0(subcirc_rambank_5_s0));  // open: D3, D2, D1, D0, WE
  SUBCIRC_RAMBank subcirc_rambank_6 (
    .Address(RAM_B_ADDRESS), .OE(1'b1), .CLK(CLOCK_GLOBAL), .S3(subcirc_rambank_6_s3),
    .S2(subcirc_rambank_6_s2), .S1(subcirc_rambank_6_s1), .S0(subcirc_rambank_6_s0));  // open: D3, D2, D1, D0, WE
  SUBCIRC_RAMBank subcirc_rambank_7 (
    .Address(RAM_B_ADDRESS), .OE(1'b1), .CLK(CLOCK_GLOBAL), .S3(subcirc_rambank_7_s3),
    .S2(subcirc_rambank_7_s2), .S1(subcirc_rambank_7_s1), .S0(subcirc_rambank_7_s0));  // open: D3, D2, D1, D0, WE
  SUBCIRC_RAMBank subcirc_rambank_8 (
    .Address(RAM_B_ADDRESS), .OE(1'b1), .CLK(CLOCK_GLOBAL), .S3(subcirc_rambank_8_s3),
    .S2(subcirc_rambank_8_s2), .S1(subcirc_rambank_8_s1), .S0(subcirc_rambank_8_s0));  // open: D3, D2, D1, D0, WE
  // Probe on subcirc_matrixadder_1_s2
  // Probe on subcirc_matrixadder_1_s0
  Register #(.width(16)) register_1 (.D(RAM_S_ADDRESS), .en(1'b1), .Q(register_1_q), .clk(CLOCK_GLOBAL));  // open: clr
  // Probe on subcirc_rambank_5_s0
  TEST_SUBCIRC_MatrixMultiplier test_subcirc_matrixmultiplier_1 (
    .B3(subcirc_rambank_5_s3), .B2(subcirc_rambank_5_s2), .B1(subcirc_rambank_5_s1),
    .B0(subcirc_rambank_5_s0), .A3(subcirc_rambank_1_s3), .A2(subcirc_rambank_1_s2),
    .A1(subcirc_rambank_1_s1), .A0(subcirc_rambank_1_s0), .S0(test_subcirc_matrixmultiplier_1_s0),
    .W0(test_subcirc_matrixmultiplier_1_w0), .S1(test_subcirc_matrixmultiplier_1_s1),
    .W1(test_subcirc_matrixmultiplier_1_w1), .S2(test_subcirc_matrixmultiplier_1_s2),
    .W2(test_subcirc_matrixmultiplier_1_w2), .S3(test_subcirc_matrixmultiplier_1_s3),
    .W3(test_subcirc_matrixmultiplier_1_w3));
  SUBCIRC_MatrixAdder subcirc_matrixadder_2 (
    .B0(test_subcirc_matrixmultiplier_1_s0), .A0(test_subcirc_matrixmultiplier_1_w0),
    .B1(test_subcirc_matrixmultiplier_1_s1), .A1(test_subcirc_matrixmultiplier_1_w1),
    .B2(test_subcirc_matrixmultiplier_1_s2), .A2(test_subcirc_matrixmultiplier_1_w2),
    .B3(test_subcirc_matrixmultiplier_1_s3), .A3(test_subcirc_matrixmultiplier_1_w3),
    .S0(subcirc_matrixadder_2_s0), .S1(subcirc_matrixadder_2_s1), .S2(subcirc_matrixadder_2_s2),
    .S3(subcirc_matrixadder_2_s3));
  TEST_SUBCIRC_MatrixMultiplier test_subcirc_matrixmultiplier_2 (
    .B3(subcirc_rambank_6_s3), .B2(subcirc_rambank_6_s2), .B1(subcirc_rambank_6_s1),
    .B0(subcirc_rambank_6_s0), .A3(subcirc_rambank_2_s3), .A2(subcirc_rambank_2_s2),
    .A1(subcirc_rambank_2_s1), .A0(subcirc_rambank_2_s0), .S0(test_subcirc_matrixmultiplier_2_s0),
    .W0(test_subcirc_matrixmultiplier_2_w0), .S1(test_subcirc_matrixmultiplier_2_s1),
    .W1(test_subcirc_matrixmultiplier_2_w1), .S2(test_subcirc_matrixmultiplier_2_s2),
    .W2(test_subcirc_matrixmultiplier_2_w2), .S3(test_subcirc_matrixmultiplier_2_s3),
    .W3(test_subcirc_matrixmultiplier_2_w3));
  SUBCIRC_MatrixAdder subcirc_matrixadder_3 (
    .B0(test_subcirc_matrixmultiplier_2_s0), .A0(test_subcirc_matrixmultiplier_2_w0),
    .B1(test_subcirc_matrixmultiplier_2_s1), .A1(test_subcirc_matrixmultiplier_2_w1),
    .B2(test_subcirc_matrixmultiplier_2_s2), .A2(test_subcirc_matrixmultiplier_2_w2),
    .B3(test_subcirc_matrixmultiplier_2_s3), .A3(test_subcirc_matrixmultiplier_2_w3),
    .S0(subcirc_matrixadder_3_s0), .S1(subcirc_matrixadder_3_s1), .S2(subcirc_matrixadder_3_s2),
    .S3(subcirc_matrixadder_3_s3));
  TEST_SUBCIRC_MatrixMultiplier test_subcirc_matrixmultiplier_3 (
    .B3(subcirc_rambank_7_s3), .B2(subcirc_rambank_7_s2), .B1(subcirc_rambank_7_s1),
    .B0(subcirc_rambank_7_s0), .A3(subcirc_rambank_3_s3), .A2(subcirc_rambank_3_s2),
    .A1(subcirc_rambank_3_s1), .A0(subcirc_rambank_3_s0), .S0(test_subcirc_matrixmultiplier_3_s0),
    .W0(test_subcirc_matrixmultiplier_3_w0), .S1(test_subcirc_matrixmultiplier_3_s1),
    .W1(test_subcirc_matrixmultiplier_3_w1), .S2(test_subcirc_matrixmultiplier_3_s2),
    .W2(test_subcirc_matrixmultiplier_3_w2), .S3(test_subcirc_matrixmultiplier_3_s3),
    .W3(test_subcirc_matrixmultiplier_3_w3));
  SUBCIRC_MatrixAdder subcirc_matrixadder_4 (
    .B0(test_subcirc_matrixmultiplier_3_s0), .A0(test_subcirc_matrixmultiplier_3_w0),
    .B1(test_subcirc_matrixmultiplier_3_s1), .A1(test_subcirc_matrixmultiplier_3_w1),
    .B2(test_subcirc_matrixmultiplier_3_s2), .A2(test_subcirc_matrixmultiplier_3_w2),
    .B3(test_subcirc_matrixmultiplier_3_s3), .A3(test_subcirc_matrixmultiplier_3_w3),
    .S0(subcirc_matrixadder_4_s0), .S1(subcirc_matrixadder_4_s1), .S2(subcirc_matrixadder_4_s2),
    .S3(subcirc_matrixadder_4_s3));
  TEST_SUBCIRC_MatrixMultiplier test_subcirc_matrixmultiplier_4 (
    .B3(subcirc_rambank_8_s3), .B2(subcirc_rambank_8_s2), .B1(subcirc_rambank_8_s1),
    .B0(subcirc_rambank_8_s0), .A3(subcirc_rambank_4_s3), .A2(subcirc_rambank_4_s2),
    .A1(subcirc_rambank_4_s1), .A0(subcirc_rambank_4_s0), .S0(test_subcirc_matrixmultiplier_4_s0),
    .W0(test_subcirc_matrixmultiplier_4_w0), .S1(test_subcirc_matrixmultiplier_4_s1),
    .W1(test_subcirc_matrixmultiplier_4_w1), .S2(test_subcirc_matrixmultiplier_4_s2),
    .W2(test_subcirc_matrixmultiplier_4_w2), .S3(test_subcirc_matrixmultiplier_4_s3),
    .W3(test_subcirc_matrixmultiplier_4_w3));
  SUBCIRC_MatrixAdder subcirc_matrixadder_5 (
    .B0(test_subcirc_matrixmultiplier_4_s0), .A0(test_subcirc_matrixmultiplier_4_w0),
    .B1(test_subcirc_matrixmultiplier_4_s1), .A1(test_subcirc_matrixmultiplier_4_w1),
    .B2(test_subcirc_matrixmultiplier_4_s2), .A2(test_subcirc_matrixmultiplier_4_w2),
    .B3(test_subcirc_matrixmultiplier_4_s3), .A3(test_subcirc_matrixmultiplier_4_w3),
    .S0(subcirc_matrixadder_5_s0), .S1(subcirc_matrixadder_5_s1), .S2(subcirc_matrixadder_5_s2),
    .S3(subcirc_matrixadder_5_s3));
  Clock clock_1 (.out(CLOCK_GLOBAL));
  TEST_SUBCIRC_MatrixAdder test_subcirc_matrixadder_1 (
    .B0(subcirc_matrixadder_2_s0), .B1(subcirc_matrixadder_2_s1), .B2(subcirc_matrixadder_2_s2),
    .B3(subcirc_matrixadder_2_s3), .A0(subcirc_matrixadder_3_s0), .A1(subcirc_matrixadder_3_s1),
    .A2(subcirc_matrixadder_3_s2), .A3(subcirc_matrixadder_3_s3), .S0(test_subcirc_matrixadder_1_s0),
    .S1(test_subcirc_matrixadder_1_s1), .S2(test_subcirc_matrixadder_1_s2), .S3(test_subcirc_matrixadder_1_s3));
  TEST_SUBCIRC_MatrixAdder test_subcirc_matrixadder_2 (
    .B0(subcirc_matrixadder_4_s0), .B1(subcirc_matrixadder_4_s1), .B2(subcirc_matrixadder_4_s2),
    .B3(subcirc_matrixadder_4_s3), .A0(subcirc_matrixadder_5_s0), .A1(subcirc_matrixadder_5_s1),
    .A2(subcirc_matrixadder_5_s2), .A3(subcirc_matrixadder_5_s3), .S0(test_subcirc_matrixadder_2_s0),
    .S1(test_subcirc_matrixadder_2_s1), .S2(test_subcirc_matrixadder_2_s2), .S3(test_subcirc_matrixadder_2_s3));
  TEST_SUBCIRC_MatrixAdder test_subcirc_matrixadder_3 (
    .B0(test_subcirc_matrixadder_1_s0), .B1(test_subcirc_matrixadder_1_s1),
    .B2(test_subcirc_matrixadder_1_s2), .B3(test_subcirc_matrixadder_1_s3),
    .A0(test_subcirc_matrixadder_2_s0), .A1(test_subcirc_matrixadder_2_s1),
    .A2(test_subcirc_matrixadder_2_s2), .A3(test_subcirc_matrixadder_2_s3), .S0(S0), .S1(S1), .S2(S2), .S3(S3));
  SUBCIRC_RAMBankOutput subcirc_rambankoutput_1 (
    .D3(S3), .D2(S2), .D1(S1), .D0(S0), .Address(register_1_q), .WE(1'b1), .CLK(CLOCK_GLOBAL),
    .S3(subcirc_rambankoutput_1_s3), .S2(subcirc_rambankoutput_1_s2), .S1(subcirc_rambankoutput_1_s1),
    .S0(subcirc_rambankoutput_1_s0));  // open: OE
  // Probe on S0
  // Probe on S2
  // Probe on S1
  // Probe on S3
  assign bit_extender_1_out = {{8{counter_4_q[7]}}, counter_4_q};  // Bit_Extender bit_extender_1
  Counter counter_4 (.Q(counter_4_q));  // open: load, D, count, carry, up, clk, clr
  assign bit_extender_2_out = {{8{counter_5_q[7]}}, counter_5_q};  // Bit_Extender bit_extender_2
  Counter counter_5 (.Q(counter_5_q));  // open: load, D, count, carry, up, clk, clr
  Comparator #(.width(16)) comparator_1 (
    .a(bit_extender_1_out), .b(ROW_ITERCOUNT), .eq(comparator_1_eq));  // open: gt, lt
  Comparator #(.width(16)) comparator_2 (
    .a(bit_extender_2_out), .b(COL_ITERCOUNT), .eq(comparator_2_eq));  // open: gt, lt
  ROM #(.dataWidth(16)) rom_1 (.addr({8{1'b0}}), .data(ROW_ITERCOUNT));
  ROM #(.dataWidth(16)) rom_2 (.addr({8{1'b0}}), .data(COL_ITERCOUNT));

  // Notes on the sheet:
  //   Pipelined
  //   RAM A Addresses
  //   Constant High Bit
  //   RAM B Addresses
  //   Row[0][0]
  //   Row[0][1]
  //   Row[0][2]
  //   Row[0][3]
  //   A
  //   A
  //   Col[0][0]
  //   Col[0][1]
  //   Col[0][2]
  //   Col[0][3]
  //   B
  //   B
  //   AW
  //   BY
  //   O
  //   Control Unit
  //   contents of rom_1 (hex, n*v repeats v):
  //   1
  //   contents of rom_2 (hex, n*v repeats v):
  //   4
  //   Configuration RAM, Holds Matrix Size (N/4)[0], Data Type (0: int64, 1: float64)[1]
endmodule
